# Fritzing sketch DoorBell (saved by Fritzing 0.9.2b)
circuit board: 4.00224cm x 5.9998cm

parts:
  SPKR1 = Loudspeaker
  Main_Board = ESP32 - CAM
  J1 = Power Jack [package=power_jack_slot]
  PIR1 = PIR sensor
  FC-1 = Sound Sensor
  PUSH_BUTTON = SWITCH-MOMENTARY-2 [package=tactile-pth-12mm]

nets (from the schematic view):
  N1: SPKR1.pin1, Main_Board.IO14
  GND: SPKR1.pin2, Main_Board.GND, J1.GND, PUSH_BUTTON.2
  N2: Main_Board.5V, J1.PWR
  N3: Main_Board.IO12, PUSH_BUTTON.1
  N4: Main_Board.IO13, FC-1.OUT
  N5: Main_Board.IO15, PIR1.SIG
  3V3: Main_Board.3V3, PIR1.VDD
  GND_2: PIR1.GND, FC-1.GND

custom parts:
  ESP32 - CAM: The ESP32-CAM has a very competitive small-size camera module that can operate independently as a minimum system with a footprint of only 27*40.5*4.5mm and a deep sleep current of up to 6mA.

// code stored in the sketch: SmartDoorbell_V1.ino
#include <String>
#include "esp_camera.h"
#include <WiFi.h>
#include <EEPROM.h>
#include <ArduinoJson.h>


#define EEPROM_SIZE 512


#define CAMERA_MODEL_AI_THINKER // Has PSRAM
#include "camera_pins.h"

#include "qrscan.h"
void QRCodeReader( void * pvParameters );

void EEPROM_put(char add, String data);
String EEPROM_get(char add);

const int JSON_BUFFER_SIZE = 256;

int metaAddress = 0;
int metaLenght = 4;
int jsonAddress = 4;

String value = "";
String WifiPassword = "";
String WifiSSID = "";

int WifiTimout = 50;


void setup() {
  Serial.begin(115200);
  EEPROM.begin(EEPROM_SIZE);
  DynamicJsonDocument jsonDoc(EEPROM_SIZE);
  setEEPROM_JSON(jsonDoc);

}

void qrSetup();

void loop() {
  DynamicJsonDocument jsonDoc = getEEPROM_JSON();


  //FOR DEBUGGING ONLY
  if (Serial.available()) {
    String SerialTemp = Serial.readString();
    if (SerialTemp = "WifiStat"){
      Serial.println("SSID = " + WifiSSID);
      Serial.println("Password = " + WifiPassword);
    }
  }

  //try to connect to Wifi, when The SSID and Password is not blank
  if (jsonDoc["WifiPassword"].as<String>() != "" && jsonDoc["WifiSSID"].as<String>() != "") {
    if(jsonDoc["WifiPassword"] == "none"){
      WifiPassword = "";
    }else {
      WifiPassword = jsonDoc["WifiPassword"].as<String>();
    }
  WifiSSID = jsonDoc["WifiSSID"].as<String>();
    WiFi.begin(WifiSSID, WifiPassword);
    WiFi.setSleep(false);

    //waiting loop to connect WiFi
    for (int c = 0; WiFi.status() != WL_CONNECTED && c <= WifiTimout; c++) {
      delay(500);
      Serial.print(".");
      Serial.println(c);
    }
    Serial.println("");
  }
  if (WiFi.status() == WL_CONNECTED){
    Serial.println("");
    Serial.println("WiFi connected");

  }else if (WiFi.status() != WL_CONNECTED){
    WiFi.disconnect(true);
    WiFi.mode(WIFI_OFF); 
    jsonDoc["WifiSSID"] = "";
    jsonDoc["WifiPassword"] = "";
    setEEPROM_JSON(jsonDoc);
    Serial.println("Wifi Connection Error");
  }

  WiFi.disconnect(true);
  

  delay(20);
}



String EEPROM_read(int index, int length) {
  String text = "";
  char ch = 1;

  for (int i = index; (i < (index + length)) && ch; ++i) {
    if (ch = EEPROM.read(i)) {
      text.concat(ch);
    }
  }
  return text;
}

int EEPROM_write(int index, String text) {
  for (int i = index; i < text.length() + index; ++i) {
    EEPROM.write(i, text[i - index]);
  }
  EEPROM.write(index + text.length(), 0);
  EEPROM.commit();

  return text.length() + 1;
}

DynamicJsonDocument getEEPROM_JSON() {

  String jsonRead = EEPROM_read(jsonAddress,
                                EEPROM_read(metaAddress, metaLenght).toInt());

  // Serial.print("JSON Read: ");
  // Serial.println(jsonRead);

  DynamicJsonDocument jsonDoc(EEPROM_SIZE);

  deserializeJson(jsonDoc, jsonRead);

  return jsonDoc;
}

void setEEPROM_JSON(DynamicJsonDocument jsonDoc) {

  String jsonWriteString;

  serializeJson(jsonDoc, jsonWriteString);

  // Serial.print("JSON Write: ");
  // Serial.println(jsonWriteString);

  EEPROM_write(metaAddress,(String)EEPROM_write(jsonAddress, jsonWriteString));
}

// code stored in the sketch: Untitled.ino

